// Logisim project cofre509771.circ as structural Verilog: 8 circuits, main circuit main
module main (
);

  wire cofre_1_aberto, cofre_1_erro, Enter_out, I1_out, I2_out, I3_out, I4_out, I5_out, I6_out, I7_out,
       I8_out, I9_out, Porta_out;

  Button I1 (.out(I1_out));
  Button I2 (.out(I2_out));
  Button I3 (.out(I3_out));
  Button I4 (.out(I4_out));
  Button I5 (.out(I5_out));
  Button I6 (.out(I6_out));
  Button I7 (.out(I7_out));
  Button I8 (.out(I8_out));
  Button I9 (.out(I9_out));
  Button Enter (.out(Enter_out));
  Button Porta (.out(Porta_out));
  LED led_1 (.in(cofre_1_aberto));
  Cofre cofre_1 (
    .i1(I1_out), .i2(I2_out), .i3(I3_out), .i4(I4_out), .i5(I5_out), .i6(I6_out), .i7(I7_out), .i8(I8_out),
    .i9(I9_out), .enter(Enter_out), .porta(Porta_out), .aberto(cofre_1_aberto), .erro(cofre_1_erro));
  LED led_2 (.in(cofre_1_erro));
endmodule

module decToBin (
  input  i1,
  input  i2,
  input  i3,
  input  i4,
  input  i5,
  input  i6,
  input  i7,
  input  i8,
  input  i9,
  output A,
  output B,
  output C,
  output D
);

  or or_1 (A, i9, i8);
  or or_2 (B, i4, i5, i6, i7);
  or or_3 (C, i2, i3, i6, i7);
  or or_4 (D, i1, i3, i5, i7, i9);
endmodule

module count (
  input  clear,
  input  i1,
  input  f1,
  input  i2,
  input  f2,
  input  i3,
  input  f3,
  input  i4,
  input  f4,
  input  i5,
  input  f5,
  input  i6,
  input  f6,
  input  i7,
  input  f7,
  input  i8,
  input  f8,
  input  i9,
  input  f9,
  output A,
  output B,
  output C,
  output D,
  output FFD
);

  wire d_ff_6_q, dectobin_1_a, dectobin_1_b, dectobin_1_c, dectobin_1_d, not_1_out, or_1_out, or_2_out,
       x1_out, x2_out, x3_out, x4_out, x5_out, x6_out, x7_out, x8_out, x9_out;

  and x1 (x1_out, i1, f1);
  and x2 (x2_out, i2, f2);
  and x3 (x3_out, i3, f3);
  and x4 (x4_out, i4, f4);
  and x5 (x5_out, i5, f5);
  and x6 (x6_out, i6, f6);
  and x7 (x7_out, i7, f7);
  and x8 (x8_out, i8, f8);
  and x9 (x9_out, i9, f9);
  D_Flip_Flop d_ff_1 (.D(dectobin_1_a), .clk(d_ff_6_q), .Q(A), .reset(clear));  // open: Qn, preset
  or or_1 (or_1_out, x1_out, x2_out, x3_out, x4_out, x5_out, x6_out, x7_out, x8_out, x9_out);
  not not_1 (not_1_out, or_1_out);
  decToBin dectobin_1 (
    .i1(x1_out), .i2(x2_out), .i3(x3_out), .i4(x4_out), .i5(x5_out), .i6(x6_out), .i7(x7_out), .i8(x8_out),
    .i9(x9_out), .A(dectobin_1_a), .B(dectobin_1_b), .C(dectobin_1_c), .D(dectobin_1_d));
  D_Flip_Flop d_ff_2 (.D(dectobin_1_b), .clk(d_ff_6_q), .Q(B), .reset(clear));  // open: Qn, preset
  D_Flip_Flop d_ff_3 (.D(d_ff_6_q), .clk(not_1_out), .Q(FFD), .reset(clear));  // open: Qn, preset
  D_Flip_Flop d_ff_4 (.D(dectobin_1_c), .clk(d_ff_6_q), .Q(C), .reset(clear));  // open: Qn, preset
  or or_2 (or_2_out, dectobin_1_a, dectobin_1_b, dectobin_1_c, dectobin_1_d);
  D_Flip_Flop d_ff_5 (.D(dectobin_1_d), .clk(d_ff_6_q), .Q(D), .reset(clear));  // open: Qn, preset
  D_Flip_Flop d_ff_6 (.D(or_2_out), .clk(or_2_out), .Q(d_ff_6_q), .reset(clear));  // open: Qn, preset
endmodule

module Cofre (
  input  i1,
  input  i2,
  input  i3,
  input  i4,
  input  i5,
  input  i6,
  input  i7,
  input  i8,
  input  i9,
  input  enter,
  input  porta,
  output aberto,
  output erro
);

  wire comparator1_1_saida, comparator2_1_saida, comparator3_1_saida, comparator4_1_saida, count_1_a,
       count_1_b, count_1_c, count_1_d, count_1_ffd, count_2_a, count_2_b, count_2_c, count_2_d, d_ff_1_q,
       d_ff_2_q, d_ff_3_q, d_ff_4_q, d_ff_5_q, dectobin_1_a, dectobin_1_b, dectobin_1_c, dectobin_1_d,
       dectobin_2_a, dectobin_2_b, dectobin_2_c, dectobin_2_d, not_1_out, not_2_out, not_3_out, or_1_out,
       or_2_out, or_3_out, or_4_out, register_1_q, register_2_q, register_3_q, register_4_q, register_5_q,
       register_6_q, register_7_q, register_8_q, register_9_q, x1_out, x2_out, x3_out, x4_out, x5_out,
       x6_out, x7_out, x8_out, x9_out;

  and x1 (x1_out, i1, d_ff_1_q);
  and x2 (x2_out, i2, d_ff_1_q);
  and x3 (x3_out, i3, d_ff_1_q);
  and x4 (x4_out, i4, d_ff_1_q);
  and x5 (x5_out, i5, d_ff_1_q);
  and x6 (x6_out, i6, d_ff_1_q);
  and x7 (x7_out, i7, d_ff_1_q);
  and x8 (x8_out, i8, d_ff_1_q);
  and x9 (x9_out, i9, d_ff_1_q);
  Register #(.width(1)) register_1 (.D(dectobin_1_a), .clk(d_ff_2_q), .Q(register_1_q), .clr(porta));  // open: en
  or or_1 (or_1_out, i1, i2, i3, i4, i5, i6, i7, i8, i9);
  D_Flip_Flop d_ff_1 (.D(d_ff_2_q), .clk(not_1_out), .Q(d_ff_1_q), .reset(porta));  // open: Qn, preset
  not not_1 (not_1_out, or_1_out);
  Register #(.width(1)) register_2 (.D(dectobin_2_a), .clk(d_ff_3_q), .Q(register_2_q), .clr(porta));  // open: en
  Register #(.width(1)) register_3 (.D(d_ff_3_q), .clk(not_2_out), .Q(register_3_q), .clr(porta));  // open: en
  or or_2 (or_2_out, x1_out, x2_out, x3_out, x4_out, x5_out, x6_out, x7_out, x8_out, x9_out);
  not not_2 (not_2_out, or_2_out);
  decToBin dectobin_1 (
    .i1(i1), .i2(i2), .i3(i3), .i4(i4), .i5(i5), .i6(i6), .i7(i7), .i8(i8), .i9(i9), .A(dectobin_1_a),
    .B(dectobin_1_b), .C(dectobin_1_c), .D(dectobin_1_d));
  Register #(.width(1)) register_4 (.D(dectobin_1_b), .clk(d_ff_2_q), .Q(register_4_q), .clr(porta));  // open: en
  Register #(.width(1)) register_5 (.D(dectobin_2_b), .clk(d_ff_3_q), .Q(register_5_q), .clr(porta));  // open: en
  Register #(.width(1)) register_6 (.D(dectobin_1_c), .clk(d_ff_2_q), .Q(register_6_q), .clr(porta));  // open: en
  decToBin dectobin_2 (
    .i1(x1_out), .i2(x2_out), .i3(x3_out), .i4(x4_out), .i5(x5_out), .i6(x6_out), .i7(x7_out), .i8(x8_out),
    .i9(x9_out), .A(dectobin_2_a), .B(dectobin_2_b), .C(dectobin_2_c), .D(dectobin_2_d));
  Register #(.width(1)) register_7 (.D(dectobin_2_c), .clk(d_ff_3_q), .Q(register_7_q), .clr(porta));  // open: en
  D_Flip_Flop d_ff_2 (.D(or_3_out), .clk(or_3_out), .Q(d_ff_2_q), .reset(porta));  // open: Qn, preset
  or or_3 (or_3_out, dectobin_1_a, dectobin_1_b, dectobin_1_c, dectobin_1_d);
  Register #(.width(1)) register_8 (.D(dectobin_1_d), .clk(d_ff_2_q), .Q(register_8_q), .clr(porta));  // open: en
  D_Flip_Flop d_ff_3 (.D(or_4_out), .clk(or_4_out), .Q(d_ff_3_q), .reset(porta));  // open: Qn, preset
  or or_4 (or_4_out, dectobin_2_a, dectobin_2_b, dectobin_2_c, dectobin_2_d);
  Register #(.width(1)) register_9 (.D(dectobin_2_d), .clk(d_ff_3_q), .Q(register_9_q), .clr(porta));  // open: en
  count count_1 (
    .clear(porta), .i1(x1_out), .f1(register_3_q), .i2(x2_out), .f2(register_3_q), .i3(x3_out),
    .f3(register_3_q), .i4(x4_out), .f4(register_3_q), .i5(x5_out), .f5(register_3_q), .i6(x6_out),
    .f6(register_3_q), .i7(x7_out), .f7(register_3_q), .i8(x8_out), .f8(register_3_q), .i9(x9_out),
    .f9(register_3_q), .A(count_1_a), .B(count_1_b), .C(count_1_c), .D(count_1_d), .FFD(count_1_ffd));
  count count_2 (
    .clear(porta), .i1(x1_out), .f1(count_1_ffd), .i2(x2_out), .f2(count_1_ffd), .i3(x3_out),
    .f3(count_1_ffd), .i4(x4_out), .f4(count_1_ffd), .i5(x5_out), .f5(count_1_ffd), .i6(x6_out),
    .f6(count_1_ffd), .i7(x7_out), .f7(count_1_ffd), .i8(x8_out), .f8(count_1_ffd), .i9(x9_out),
    .f9(count_1_ffd), .A(count_2_a), .B(count_2_b), .C(count_2_c), .D(count_2_d));  // open: FFD
  D_Flip_Flop d_ff_4 (.D(1'b1), .clk(enter), .Q(d_ff_4_q), .reset(porta));  // open: Qn, preset
  comparator1 comparator1_1 (
    .A(register_1_q), .B(register_4_q), .C(register_6_q), .D(register_8_q), .saida(comparator1_1_saida));
  comparator2 comparator2_1 (
    .A(register_2_q), .B(register_5_q), .C(register_7_q), .D(register_9_q), .saida(comparator2_1_saida));
  comparator3 comparator3_1 (.A(count_1_a), .B(count_1_b), .C(count_1_c), .D(count_1_d), .saida(comparator3_1_saida));
  comparator4 comparator4_1 (.A(count_2_a), .B(count_2_b), .C(count_2_c), .D(count_2_d), .saida(comparator4_1_saida));
  and and_1 (aberto, comparator1_1_saida, comparator2_1_saida, comparator3_1_saida, comparator4_1_saida, d_ff_4_q);
  D_Flip_Flop d_ff_5 (.D(d_ff_2_q), .clk(d_ff_2_q), .Q(d_ff_5_q), .reset(porta));  // open: Qn, preset
  not not_3 (not_3_out, aberto);
  and and_2 (erro, not_3_out, d_ff_5_q);
endmodule

module comparator1 (
  input  A,
  input  B,
  input  C,
  input  D,
  output saida
);

  wire xnor_1_out, xnor_2_out, xnor_3_out, xnor_4_out;

  xnor xnor_1 (xnor_1_out, A, 1'b1);
  xnor xnor_2 (xnor_2_out, B, 1'b0);
  xnor xnor_3 (xnor_3_out, C, 1'b0);
  xnor xnor_4 (xnor_4_out, D, 1'b1);
  and and_1 (saida, xnor_1_out, xnor_2_out, xnor_3_out, xnor_4_out);
endmodule

module comparator2 (
  input  A,
  input  B,
  input  C,
  input  D,
  output saida
);

  wire xnor_1_out, xnor_2_out, xnor_3_out, xnor_4_out;

  xnor xnor_1 (xnor_1_out, A, 1'b0);
  xnor xnor_2 (xnor_2_out, B, 1'b0);
  xnor xnor_3 (xnor_3_out, C, 1'b1);
  xnor xnor_4 (xnor_4_out, D, 1'b1);
  and and_1 (saida, xnor_1_out, xnor_2_out, xnor_3_out, xnor_4_out);
endmodule

module comparator3 (
  input  A,
  input  B,
  input  C,
  input  D,
  output saida
);

  wire xnor_1_out, xnor_2_out, xnor_3_out, xnor_4_out;

  xnor xnor_1 (xnor_1_out, A, 1'b0);
  xnor xnor_2 (xnor_2_out, B, 1'b1);
  xnor xnor_3 (xnor_3_out, C, 1'b1);
  xnor xnor_4 (xnor_4_out, D, 1'b1);
  and and_1 (saida, xnor_1_out, xnor_2_out, xnor_3_out, xnor_4_out);
endmodule

module comparator4 (
  input  A,
  input  B,
  input  C,
  input  D,
  output saida
);

  wire xnor_1_out, xnor_2_out, xnor_3_out, xnor_4_out;

  xnor xnor_1 (xnor_1_out, A, 1'b0);
  xnor xnor_2 (xnor_2_out, B, 1'b1);
  xnor xnor_3 (xnor_3_out, C, 1'b0);
  xnor xnor_4 (xnor_4_out, D, 1'b0);
  and and_1 (saida, xnor_1_out, xnor_2_out, xnor_3_out, xnor_4_out);
endmodule
