// Logisim project contadorsicronogray.circ as structural Verilog: 2 circuits, main circuit main
module main (
  input  in_1
);

  wire button_1_out, clock_1_out;
  wire [3:0] contador_1_saida;

  Button button_1 (.out(button_1_out));
  Clock clock_1 (.out(clock_1_out));
  contador contador_1 (.Start(in_1), .Reset(button_1_out), .Clk(clock_1_out), .saida(contador_1_saida));
  Hex_Digit_Display hex_digit_display_1 (.value(contador_1_saida));  // open: dp

  // Notes on the sheet:
  //   esse circuito simula um contador na sequencia de codigo gray
endmodule

module contador (
  input  Start,
  input  Reset,
  input  Clk,
  output [3:0] saida
);

  wire and_1_out, and_2_out, j_k_ff_1_q, j_k_ff_2_q, j_k_ff_3_q;

  J_K_Flip_Flop j_k_ff_1 (.J(Start), .K(Start), .clk(Clk), .Q(j_k_ff_1_q), .reset(Reset));  // open: Qn, preset
  and and_1 (and_1_out, j_k_ff_1_q, j_k_ff_2_q);
  J_K_Flip_Flop j_k_ff_2 (
    .J(j_k_ff_1_q), .K(j_k_ff_1_q), .clk(Clk), .Q(j_k_ff_2_q), .reset(Reset));  // open: Qn, preset
  J_K_Flip_Flop j_k_ff_3 (.J(and_1_out), .K(and_1_out), .clk(Clk), .Q(j_k_ff_3_q), .reset(Reset));  // open: Qn, preset
  and and_2 (and_2_out, and_1_out, j_k_ff_3_q);
  J_K_Flip_Flop j_k_ff_4 (.J(and_2_out), .K(and_2_out), .clk(Clk), .Q(saida[3]), .reset(Reset));  // open: Qn, preset
  xor xor_1 (saida[0], j_k_ff_2_q, j_k_ff_1_q);
  xor xor_2 (saida[1], j_k_ff_2_q, j_k_ff_3_q);
  xor xor_3 (saida[2], j_k_ff_3_q, saida[3]);
endmodule
