// Logisim project cronometro.circ as structural Verilog: 3 circuits, main circuit main
module main (
  input  Start_Stop
);

  wire and_1_out, clock_1_out, count_3bits_2_cout, count_4bits_1_cout, count_4bits_2_cout, Reset_out;
  wire [3:0] count_3bits_1_qn, count_3bits_2_qn, count_4bits_1_qn, count_4bits_2_qn;

  count_3bits count_3bits_1 (.CLK(count_4bits_1_cout), .RESET(Reset_out), .Qn(count_3bits_1_qn));  // open: cout
  Hex_Digit_Display #(.decimalPoint("false")) hex_digit_display_1 (.value(count_3bits_1_qn));
  Hex_Digit_Display #(.decimalPoint("false")) hex_digit_display_2 (.value(count_4bits_1_qn));
  count_4bits count_4bits_1 (
    .CLK(count_3bits_2_cout), .RESET(Reset_out), .Qn(count_4bits_1_qn), .cout(count_4bits_1_cout));
  Hex_Digit_Display #(.decimalPoint("false")) hex_digit_display_3 (.value(count_3bits_2_qn));
  Button Reset (.out(Reset_out));
  count_3bits count_3bits_2 (
    .CLK(count_4bits_2_cout), .RESET(Reset_out), .Qn(count_3bits_2_qn), .cout(count_3bits_2_cout));
  Clock clock_1 (.out(clock_1_out));
  and and_1 (and_1_out, clock_1_out, Start_Stop);
  Hex_Digit_Display #(.decimalPoint("false")) hex_digit_display_4 (.value(count_4bits_2_qn));
  count_4bits count_4bits_2 (.CLK(and_1_out), .RESET(Reset_out), .Qn(count_4bits_2_qn), .cout(count_4bits_2_cout));
endmodule

// 0.9
module count_4bits (
  input  CLK,
  input  RESET,
  output [3:0] Qn,
  output cout
);

  wire and_1_out, or_1_out;

  T_Flip_Flop #(.trigger("falling")) t_ff_1 (.T(1'b1), .clk(CLK), .Q(Qn[0]), .reset(or_1_out));  // open: Qn, preset
  T_Flip_Flop #(.trigger("falling")) t_ff_2 (.T(1'b1), .clk(Qn[0]), .Q(Qn[1]), .reset(or_1_out));  // open: Qn, preset
  T_Flip_Flop #(.trigger("falling")) t_ff_3 (.T(1'b1), .clk(Qn[1]), .Q(Qn[2]), .reset(or_1_out));  // open: Qn, preset
  T_Flip_Flop #(.trigger("falling")) t_ff_4 (.T(1'b1), .clk(Qn[2]), .Q(cout), .reset(or_1_out));  // open: Qn, preset
  or or_1 (or_1_out, and_1_out, RESET);
  and and_1 (and_1_out, ~Qn[0], Qn[1], ~Qn[2], cout);  // AND_Gate

  assign Qn[3] = cout;
endmodule

// 0.5
module count_3bits (
  input  CLK,
  input  RESET,
  output [3:0] Qn,
  output cout
);

  wire and_1_out, or_1_out;

  T_Flip_Flop #(.trigger("falling")) t_ff_1 (.T(1'b1), .clk(CLK), .Q(Qn[0]), .reset(or_1_out));  // open: Qn, preset
  T_Flip_Flop #(.trigger("falling")) t_ff_2 (.T(1'b1), .clk(Qn[0]), .Q(Qn[1]), .reset(or_1_out));  // open: Qn, preset
  T_Flip_Flop #(.trigger("falling")) t_ff_3 (.T(1'b1), .clk(Qn[1]), .Q(cout), .reset(or_1_out));  // open: Qn, preset
  T_Flip_Flop #(.trigger("falling")) t_ff_4 (.T(1'b1), .clk(cout), .Q(Qn[3]), .reset(or_1_out));  // open: Qn, preset
  or or_1 (or_1_out, and_1_out, RESET);
  and and_1 (and_1_out, ~Qn[0], Qn[1], cout, ~Qn[3]);  // AND_Gate

  assign Qn[2] = cout;
endmodule
